# Fritzing sketch Schaltplan (saved by Fritzing 0.9.2b)
circuit board: 4.5cm x 4cm
breadboards: 1

parts:
  R1 = Resistor [tolerance=±5% resistance=330 package=THT]
  R2 = Resistor [tolerance=±5% resistance=470 package=THT]
  HC-SR04 = HC-SR04 [chip_label=IC package="SIP (Single Inline) [THT]"]
  Raspberry_Pi1 = Raspberry Pi 2
  +5V_GND = male pin header, 2 pins [form="♂ (male)"]
  TRIGGER_ECHO = male pin header, 2 pins [form="♂ (male)"]

nets:
  N1: R1.Pin_0, HC-SR04.Echo
  N2: R1.Pin_1, R2.Pin_0, Raspberry_Pi1.GPIO24, TRIGGER_ECHO.pin1
  GND: R2.Pin_1, HC-SR04.GND, Raspberry_Pi1.GND, +5V_GND.pin1
  VCC: HC-SR04.Vcc, Raspberry_Pi1.5V, +5V_GND.pin2
  N3: HC-SR04.Trig, Raspberry_Pi1.GPIO18, TRIGGER_ECHO.pin2

notes:
  R1 330Ω
  R2 470Ω
  R1
  R2
  Entfernungsmesser (Rev.0)
  tfnApps.de Jens Dutzi

custom parts:
  HC-SR04: HC-SR04 ultrasound distance sensor
